# Fritzing sketch KelderPomp (saved by Fritzing 0.9.3b)

parts:
  Onderdeel1 = Arduino Uno (Rev3)
  M1 = 1 chan 5v relay module

nets:
  N1: Onderdeel1.D9_PWM, M1.pin_3
  N2: Onderdeel1.GND, M1.pin_2
  N3: Onderdeel1.5V, M1.pin_1

notes:
  230V
  Pump
  Water

custom parts:
  1 chan 5v relay module: 1 Channel 5V Relay Module Board Shield with Optocoupler Support High and Low Level Trigger for Arduino.
